# Fritzing sketch EP1 (saved by Fritzing 0.9.3b)
breadboards: 1

parts:
  Part1 = Arduino Mega 2560 (Rev3)
  J1 = Piezo Speaker
  R1 = Resistor [tolerance=±5% resistance=10k package="2010 [SMD]"]
  hc-sr1 = hc-sr04
  VCC1 = 4 x AAA Battery Mount

nets:
  N1: Part1.D8_PWM, R1.Pin_1
  GND: Part1.GND, J1.pin1, hc-sr1.GND, VCC1.-
  N2: Part1.D3_PWM, hc-sr1.Trig
  N3: Part1.D4_PWM, hc-sr1.Echo
  N4: J1.pin2, R1.Pin_0
  N5: hc-sr1.VCC, VCC1.+
