# Fritzing sketch EP2 (saved by Fritzing 0.9.3b)
breadboards: 1

parts:
  U1 = QRE1113 [package=qre1113]
  Arduino_Mega = Arduino Mega 2560 (Rev3)
  LED1 = smd LED [color="Red (633nm)" package="0603 [SMD]"]
  VCC1 = 4 x AAA Battery Mount
  R1 = Resistor [tolerance=±5% resistance=220 package="2010 [SMD]"]
  R2 = Resistor [tolerance=±5% resistance=130 package="2010 [SMD]"]
  R3 = Resistor [tolerance=±5% resistance=10k package="2010 [SMD]"]

nets:
  N1: U1.A, R2.Pin_0
  N2: U1.K, U1.E, Arduino_Mega.GND, LED1.cathode, VCC1.-
  N3: U1.C, Arduino_Mega.A0, R3.Pin_0
  N4: Arduino_Mega.D13_PWM, R1.Pin_0
  N5: LED1.anode, R1.Pin_1
  N6: VCC1.+, R2.Pin_1, R3.Pin_1
