# Fritzing sketch EP3 (saved by Fritzing 0.9.3b)
breadboards: 1

parts:
  R1 = Temperature Sensor (Thermistor) [thermistor_type=NTC package=THT]
  VCC1 = 4 x AAA Battery Mount
  R = Resistor [tolerance=±5% resistance=3.6k package=THT]
  R1_2 = Resistor [tolerance=±5% resistance=1.5k package=THT]
  R2 = Resistor [tolerance=±5% resistance=1k package=THT]
  LED1 = LED - 5mm [color="Green (555nm)" package="5 mm [THT]"]
  LED2 = LED - 5mm [color="Yellow (585nm)" package="5 mm [THT]"]
  LED3 = LED - 5mm [color="Red (633nm)" package="5 mm [THT]"]
  Rred = Resistor [tolerance=±5% resistance=330 package=THT]
  Ryellow = Resistor [tolerance=±5% resistance=330 package=THT]
  Rgreen = Resistor [tolerance=±5% resistance=330 package=THT]
  IC1 = IC, DIP package, 8 pins [chip_label=IC]
  Arduino_Mega = Arduino Mega 2560 (Rev3)

nets:
  N1: R1.pin_0, R.Pin_0, IC1.pin3
  N2: R1.pin_1, VCC1.+, IC1.pin8
  N3: VCC1.-, R.Pin_1, R1_2.Pin_1, LED1.cathode, LED2.cathode, LED3.cathode, IC1.pin4, Arduino_Mega.GND
  N4: R1_2.Pin_0, R2.Pin_0, IC1.pin2
  N5: R2.Pin_1, IC1.pin1, Arduino_Mega.A1
  N6: LED1.anode, Rgreen.Pin_0
  N7: LED2.anode, Ryellow.Pin_0
  N8: LED3.anode, Rred.Pin_0
  N9: Rred.Pin_1, Arduino_Mega.D10_PWM
  N10: Ryellow.Pin_1, Arduino_Mega.D11_PWM
  N11: Rgreen.Pin_1, Arduino_Mega.D12_PWM
