# Fritzing sketch EP1 (saved by Fritzing 0.9.3b)
breadboards: 1

parts:
  J1 = Piezo Speaker
  R1 = Resistor [tolerance=±5% resistance=10k package="2010 [SMD]"]
  hc-sr1 = hc-sr04
  VCC1 = 4 x AAA Battery Mount
  Part1 = Arduino Mega 2560 (Rev3)

nets:
  GND: J1.pin1, hc-sr1.GND, VCC1.-, Part1.GND
  N1: J1.pin2, R1.Pin_0
  N2: R1.Pin_1, Part1.D4_PWM
  N3: hc-sr1.VCC, VCC1.+
  N4: hc-sr1.Trig, Part1.D2_PWM
  N5: hc-sr1.Echo, Part1.D3_PWM
