# Fritzing sketch EP1F (saved by Fritzing 0.9.3b)
breadboards: 2

parts:
  J1 = Piezo Speaker
  R1 = Resistor [tolerance=±5% resistance=10k package="2010 [SMD]"]
  hc-sr1 = hc-sr04
  VCC1 = 4 x AAA Battery Mount
  Part1 = Arduino Mega 2560 (Rev3)
  TFT1 = Color 320x240 TFT Display, ILI9341 Controller Chip
  R2 = Resistor [tolerance=±5% resistance=1k package="2512 [SMD]"]
  R3 = Resistor [tolerance=±5% resistance=2k package="2512 [SMD]"]
  R4 = Resistor [tolerance=±5% resistance=1k package="2512 [SMD]"]
  R5 = Resistor [tolerance=±5% resistance=1k package="2512 [SMD]"]
  R6 = Resistor [tolerance=±5% resistance=1k package="2512 [SMD]"]
  R7 = Resistor [tolerance=±5% resistance=2k package="1206 [SMD]"]
  R8 = Resistor [tolerance=±5% resistance=2k package="1206 [SMD]"]
  R9 = Resistor [tolerance=±5% resistance=2k package="1206 [SMD]"]
  R10 = Resistor [tolerance=±5% resistance=10k package="1206 [SMD]"]

nets:
  GND: J1.pin1, hc-sr1.GND, VCC1.-, Part1.GND, TFT1.GND, R3.Pin_0, R7.Pin_0, R8.Pin_0, R9.Pin_0
  N1: J1.pin2, R1.Pin_0
  N2: R1.Pin_1, Part1.D4_PWM
  N3: hc-sr1.VCC, VCC1.+
  N4: hc-sr1.Trig, Part1.D2_PWM
  N5: hc-sr1.Echo, Part1.D3_PWM
  3V3: Part1.3V3, TFT1.VCC, TFT1.Reset, R10.Pin_1
  N6: Part1.D49, R4.Pin_1
  N7: Part1.D50, TFT1.SDO_(MISO)
  N8: Part1.D51, R5.Pin_1
  N9: Part1.D52, R6.Pin_1
  N10: Part1.D53, R2.Pin_1
  N11: TFT1.CS, R2.Pin_0, R3.Pin_1
  N12: TFT1.D/C, R4.Pin_0, R7.Pin_1
  N13: TFT1.SDI_(MOSI), R5.Pin_0, R8.Pin_1
  N14: TFT1.SCK, R6.Pin_0, R9.Pin_1
  N15: TFT1.LED, R10.Pin_0

custom parts:
  Color 320x240 TFT Display, ILI9341 Controller Chip: 2.2" TFT Display with ILI9341 Controller
